# Fritzing sketch simon (saved by Fritzing 0.9.3b)
breadboards: 1

parts:
  LCD1 = LCD screen
  Part1 = Arduino Uno (Rev3)
  R2 = Resistor [tolerance=±5% resistance=220 package=THT]
  LED1 = LED - 5mm [color="Green (555nm)" package="5 mm [THT]"]
  R3 = Resistor [tolerance=±5% resistance=220 package=THT]
  LED2 = LED - 5mm [color="Red (633nm)" package="5 mm [THT]"]
  R4 = Resistor [tolerance=±5% resistance=220 package=THT]
  J3 = Piezo Speaker
  J4 = Basic Force Sensing Resistor (FSR) [package=THT]
  R5 = Resistor [tolerance=±5% resistance=220 package=THT]
  LED3 = LED - 5mm [color="Yellow (585nm)" package="5 mm [THT]"]
  J5 = Basic Force Sensing Resistor (FSR) [package=THT]
  LED4 = LED - 5mm [color="Blue (430nm)" package="5 mm [THT]"]
  R6 = Resistor [tolerance=±5% resistance=220 package=THT]
  U1 = POT [package=3362u]
  R7 = Resistor [tolerance=±5% resistance=1M package=THT]
  R8 = Resistor [tolerance=±5% resistance=1M package=THT]

nets:
  VSS: LCD1.VSS, Part1.GND, R2.Pin_1, R3.Pin_1, R4.Pin_1, J4.pin_0, R5.Pin_1, J5.pin_0, R6.Pin_1, U1.A
  VDD: LCD1.VDD, Part1.5V, U1.E
  N1: LCD1.V0, U1.S
  N2: LCD1.RS, Part1.A0
  N3: LCD1.E, Part1.A1
  N4: LCD1.DB4, Part1.A2
  N5: LCD1.DB5, Part1.A3
  N6: LCD1.DB6, Part1.A4/SDA
  N7: LCD1.DB7, Part1.A5/SCL
  N8: Part1.D8, J3.pin2
  N9: Part1.D9_PWM, LED2.anode
  N10: Part1.D10_PWM/SS, R8.Pin_1
  N11: Part1.D11_PWM/MOSI, R7.Pin_0
  N12: Part1.D12/MISO, LED1.anode
  N13: Part1.D13/SCK, R7.Pin_1
  N14: Part1.D2, LED4.anode
  N15: Part1.D3_PWM, J5.pin_1
  N16: Part1.D5_PWM, LED3.anode
  N17: Part1.D6_PWM, J4.pin_1
  N18: Part1.D7, R8.Pin_0
  N19: R2.Pin_0, LED2.cathode
  N20: LED1.cathode, R3.Pin_0
  N21: R4.Pin_0, J3.pin1
  N22: R5.Pin_0, LED3.cathode
  N23: LED4.cathode, R6.Pin_0

notes:
  CONDUCTIVE FABRIC
